// Digital circuit ALU_main.dig as structural Verilog
module ALU_main (
  input  [7:0] A_in,
  input  [7:0] B_in,
  input  [2:0] ALU_op,
  input  CLK,
  input  START,
  output [7:0] S_out,
  output Z_flag
);

  wire [3:0] Q_div;
  wire [7:0] P_mult, S_ALU;

  ALU_v1 alu_v1_1 (.A_in(A_in), .B_in(B_in), .Op_Sel(ALU_op[1:0]), .S(S_ALU));
  // divider_4bit divider_4bit_1: pin names not known; wires that end beside it: A_in[3:0], B_in[3:0], CLK, START, Q_div
  multiplier_4bit multiplier_4bit_1 (.A_in(A_in[3:0]), .B_in(B_in[3:0]), .CLK(CLK), .START(START), .P_out(P_mult));
  Multiplexer #(.Bits(8), .Selector_Bits(3)) multiplexer_1 (
    .sel(ALU_op), .in_0(S_ALU), .in_1(S_ALU), .in_2(S_ALU), .in_3(S_ALU), .in_4(P_mult),
    .in_5({4'b0000, Q_div}), .in_6({8{1'b0}}), .in_7({8{1'b0}}), .out(S_out));
  nor nor_1 (Z_flag, S_out[0], S_out[1], S_out[2], S_out[3], S_out[4], S_out[5], S_out[6], S_out[7]);
endmodule
