// Digital circuit adder_4bit.dig as structural Verilog
module adder_4bit (
  input  [3:0] A,
  input  [3:0] B,
  input  Cin,
  output [3:0] Sum,
  output Cout
);

  wire full_adder_1_p4, full_adder_2_p2, full_adder_3_p2;

  // full_adder full_adder_1: pin names not known; wires that end beside it: A, B, Cin, full_adder_1_p4
  // full_adder full_adder_2: pin names not known; wires that end beside it: full_adder_1_p4, full_adder_2_p2
  // full_adder full_adder_3: pin names not known; wires that end beside it: full_adder_2_p2, full_adder_3_p2
  // full_adder full_adder_4: pin names not known; wires that end beside it: full_adder_3_p2, Sum, Cout
endmodule
