// Digital circuit multiplier_4bit.dig as structural Verilog
module multiplier_4bit (
  input  [3:0] A,
  input  [3:0] B,
  input  CLK,
  input  in_5,
  output [7:0] P
);

  wire and_1_out, and_2_out, and_3_out, counter_4bit_1_zero, d_ff_as_1_nq, d_ff_as_1_q, not_1_out, not_2_out,
       or_1_out;
  wire [7:0] adder_8bit_1_s, bitextender_1_out;

  and and_1 (and_1_out, CLK, d_ff_as_1_q);
  D_FF_AS #(.Bits(8)) P_reg (.Set(1'b0), .D(adder_8bit_1_s), .C(and_1_out), .Clr(and_3_out), .Q(P));  // open: nQ
  Button START ();  // open: out
  BitExtender #(.inputBits(4), .outputBits(8)) bitextender_1 (.in(A), .out(bitextender_1_out));
  counter_4bit counter_4bit_1 (
    .D(B), .CLK(CLK), .LOAD(and_3_out), .EN(d_ff_as_1_q), .ZERO(counter_4bit_1_zero));  // open: Q
  not not_1 (not_1_out, counter_4bit_1_zero);
  adder_8bit adder_8bit_1 (.A(P), .B(bitextender_1_out), .Cin(1'b0), .S(adder_8bit_1_s));  // open: Cout
  D_FF_AS d_ff_as_1 (.Set(1'b0), .D(or_1_out), .C(CLK), .Clr(1'b0), .Q(d_ff_as_1_q), .nQ(d_ff_as_1_nq));
  not not_2 (not_2_out, d_ff_as_1_q);
  and and_2 (and_2_out, not_1_out, d_ff_as_1_q);
  and and_3 (and_3_out, not_2_out, in_5);
  LED DONE (.in(d_ff_as_1_nq));
  or or_1 (or_1_out, and_2_out, in_5);
endmodule
